# Fritzing sketch bb_full (saved by Fritzing 1.0.6)
breadboards: 4

parts:
  OLED2 = OLED 128x64 I2C Monochrome Display GND-VDD
  A9 = Esp32-c3 super mini
  OLED6 = OLED 128x64 I2C Monochrome Display GND-VDD
  A12 = Esp32-c3 super mini
  OLED7 = OLED 128x64 I2C Monochrome Display GND-VDD  # not connected
  OLED8 = OLED 128x64 I2C Monochrome Display GND-VDD
  A14 = Esp32-c3 super mini
  OLED9 = OLED 128x64 I2C Monochrome Display GND-VDD
  A15 = Esp32-c3 super mini
  MCU1 = Wemos Lolin32lite  # not connected

nets:
  N1: OLED2.GND, A9.Pin_15
  N2: OLED2.VDD, A9.Pin_14
  N3: OLED2.SCK, A9.Pin_6
  N4: OLED2.SDA, A9.Pin_12
  N5: OLED6.GND, A12.Pin_15
  N6: OLED6.VDD, A12.Pin_14
  N7: OLED6.SCK, A12.Pin_6
  N8: OLED6.SDA, A12.Pin_12
  N9: OLED8.VDD, A14.Pin_14
  N10: OLED8.SCK, A14.Pin_6
  N11: OLED8.SDA, A14.Pin_12
  N12: OLED9.VDD, A15.Pin_14
  N13: OLED9.SCK, A15.Pin_6
  N14: OLED9.SDA, A15.Pin_12

custom parts:
  OLED 128x64 I2C Monochrome Display GND-VDD: OLED 128x64 I2C Monochrome Display. Note: there are two variants of this part, this one is the GND VDD SCK SDA variant. The other is VDD GND SCK SDA. Make sure you select the part that matches your module as using the incorrect part will probably destroy your module! In addition the mounting holes are marked on silkscreen but not by default drilled. If you want drilled mounting holes, copy a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
  Esp32-c3 super mini: ESP32-C3 Development Board ESP32 SuperMini Development Board ESP32 Development Board WiFi Bluetooth.
  Wemos Lolin32lite: Wemos Lolinlite32 wifi and blue tooth board based on the ESP-32 cpu, digital I/Os 19, analog inputs 6, clock 240mhz, Flash 4Mbytes, lipo battery charger (500ma connection broken out on breadboard but not pcb), usb.
